# Fritzing sketch LED_RGB (saved by Fritzing 0.9.0b)
breadboards: 1

parts:
  R1 = Resistor [tolerance=±5% resistance=220 package=THT]
  Componente1 = Arduino Uno (Rev3)
  R2 = Resistor [tolerance=±5% resistance=220 package=THT]
  LED1 = RGB LED (com. cathode, rgb) [package="5 mm [THT]"]
  R3 = Resistor [tolerance=±5% resistance=220 package=THT]

nets:
  N1: R1.Pin_0, LED1.green_anode
  N2: R1.Pin_1, Componente1.D10_PWM/SS
  N3: Componente1.D9_PWM, R2.Pin_0
  N4: Componente1.D11_PWM/MOSI, R3.Pin_1
  N5: Componente1.GND, LED1.common_cathode
  N6: R2.Pin_1, LED1.red_anode
  N7: LED1.blue_anode, R3.Pin_0
