# Fritzing sketch led_aceso_com_botao_tactil (saved by Fritzing 0.9.0b)
breadboards: 1

parts:
  R1 = Resistor [tolerance=±5% resistance=220 package=THT]
  Componente1 = Arduino Uno (Rev3)
  LED1 = LED - 5mm [color="Red (633nm)" package="5 mm [THT]"]  # not connected
  S1 = Pushbutton [package="[THT]"]

nets:
  N1: R1.Pin_1, S1.Pin_3, S1.Pin_4
  N2: Componente1.GND, S1.Pin_1, S1.Pin_2
