# Fritzing sketch laser (saved by Fritzing 0.9.0b)
breadboards: 1

parts:
  Q1 = PNP-Transistor [package="TO92 [THT]"]
  Componente1 = Arduino Uno (Rev3)

nets:
  N1: Q1.E, Componente1.D2
  N2: Q1.B, Componente1.5V
  N3: Q1.C, Componente1.GND

notes:
  Laser pinos:
  esq meio direita
  S alimentação - GND
