# Fritzing sketch leitura_analogica_potenciometro_com_led_alterando_delay (saved by Fritzing 0.9.0b)
breadboards: 1

parts:
  Componente1 = Arduino Uno (Rev3)
  R1 = Rotary Potentiometer (Large) [maximum_resistance=100kΩ package=THT]
  LED1 = LED - 5mm [color="Red (633nm)" package="5 mm [THT]"]  # not connected
  R2 = Resistor [tolerance=±5% resistance=220 package=THT]

nets:
  N1: Componente1.A0, R1.wiper
  N2: Componente1.5V, R1.leg1
  N3: Componente1.GND, R1.leg2, R2.Pin_1
