# Fritzing sketch modulo_receptor_IR (saved by Fritzing 0.9.0b)
breadboards: 1

parts:
  Componente1 = Arduino Uno (Rev3)
  J1 = Infrared Proximity Sensor

nets:
  N1: Componente1.D2, J1.Vout
  5V: Componente1.5V, J1.Vcc
  GND: Componente1.GND, J1.GND

notes:
  módulo receptor IR
