# Fritzing sketch sensor_LDR (saved by Fritzing 0.9.0b)
breadboards: 1

parts:
  R1 = Resistor [tolerance=±5% resistance=10k package=THT]
  Componente1 = Arduino Uno (Rev3)
  R2 = Photocell (LDR) [package=THT]

nets:
  N1: R1.Pin_0, Componente1.A0, R2.pin_0
  N2: R1.Pin_1, Componente1.GND
  N3: Componente1.5V, R2.pin_1
