# Fritzing sketch sensor_LDR_com_LED (saved by Fritzing 0.9.0b)
breadboards: 1

parts:
  R1 = Resistor [tolerance=±5% resistance=10k package=THT]
  Componente1 = Arduino Uno (Rev3)
  R2 = Photocell (LDR) [package=THT]
  LED1 = LED - 5mm [color="Red (633nm)" package="5 mm [THT]"]
  R3 = Resistor [tolerance=±5% resistance=220 package=THT]

nets:
  N1: R1.Pin_0, Componente1.A0, R2.pin_0
  N2: R1.Pin_1, Componente1.GND, R3.Pin_0
  N3: Componente1.D2, LED1.anode
  N4: Componente1.5V, R2.pin_1
  N5: LED1.cathode, R3.Pin_1
