# Fritzing sketch sensor_ultrasonico (saved by Fritzing 0.9.0b)
breadboards: 1

parts:
  Componente1 = Arduino Uno (Rev3)
  Componente2 = HC-SR04 Ultrasonic Rangemeter

nets:
  N1: Componente1.D2, Componente2.Trig
  N2: Componente1.D3_PWM, Componente2.Echo
  5V: Componente1.5V, Componente2.VCC
  GND: Componente1.GND, Componente2.GND
