# Fritzing sketch tres_leds_piscando_com_array_contador_if (saved by Fritzing 0.9.0b)
breadboards: 1

parts:
  R1 = Resistor [tolerance=±5% resistance=220 package=THT]
  Componente1 = Arduino Uno (Rev3)
  LED1 = LED - 5mm [color="Red (633nm)" package="5 mm [THT]"]
  LED2 = LED - 5mm [color="Red (633nm)" package="5 mm [THT]"]
  R2 = Resistor [tolerance=±5% resistance=220 package=THT]
  R3 = Resistor [tolerance=±5% resistance=220 package=THT]  # not connected
  LED3 = LED - 5mm [color="Red (633nm)" package="5 mm [THT]"]

nets:
  N1: R1.Pin_0, LED1.anode
  N2: R1.Pin_1, Componente1.GND, R2.Pin_1
  N3: Componente1.D2, LED2.cathode
  N4: Componente1.D3_PWM, LED1.cathode
  N5: Componente1.D4, LED3.cathode
  N6: LED2.anode, R2.Pin_0
